// Digital circuit Core.dig as structural Verilog
module Core (
  input  Clock
);

  wire d_ff_1_nq, H, Line_Count_pulse, Pclk, Pixel_Count_next, Pixel_Count_pulse, V;
  wire [7:0] B_Pal_d, G_Pal_d, R_Pal_d, VRAM_d;
  wire [9:0] Line_Count_v, Pixel_Count_v, register_1_q, register_3_q;
  wire [18:0] add_1_s;
  wire [19:0] mul_1_mul;

  vga_timing Pixel_Count (
    .Pclk(Pclk), .res(10'h280), .fp(10'h10), .sync(10'h60), .bp(10'h30), .neg(1'b1), .clock(Clock),
    .en(1'b1), .V(Pixel_Count_v), .pulse(Pixel_Count_pulse), .next(Pixel_Count_next));
  vga_timing Line_Count (
    .Pclk(Pixel_Count_next), .res(10'h1e0), .fp(10'ha), .sync(10'h2), .bp(10'h21), .neg(1'b1), .clock(Clock),
    .en(1'b1), .V(Line_Count_v), .pulse(Line_Count_pulse));  // open: next
  D_FF d_ff_1 (.D(d_ff_1_nq), .C(Clock), .Q(Pclk), .nQ(d_ff_1_nq));
  Register #(.Bits(10)) register_1 (.D(Pixel_Count_v), .C(Pclk), .en(1'b1), .Q(register_1_q));
  Register register_2 (.D(Pixel_Count_pulse), .C(Pclk), .en(1'b1), .Q(H));
  Register #(.Bits(10)) register_3 (.D(Line_Count_v), .C(Pclk), .en(1'b1), .Q(register_3_q));
  Register register_4 (.D(Line_Count_pulse), .C(Pclk), .en(1'b1), .Q(V));
  Mul #(.Bits(10)) mul_1 (.a(10'h280), .b(register_3_q), .mul(mul_1_mul));
  Add #(.Bits(19)) add_1 (.a({{9{1'b0}}, register_1_q}), .b(mul_1_mul[18:0]), .c_i(1'b0), .s(add_1_s));  // open: c_o
  RAMDualPort #(.AddrBits(19), .isProgramMemory("true"), .Bits(8)) VRAM (
    .A(add_1_s), .Din({8{1'b0}}), .str(1'b0), .C(Clock), .ld(1'b1), .D(VRAM_d));
  ROM #(.AddrBits(6), .Bits(8)) R_Pal (.A(VRAM_d[5:0]), .sel(1'b1), .D(R_Pal_d));
  ROM #(.AddrBits(6), .Bits(8)) G_Pal (.A(VRAM_d[5:0]), .sel(1'b1), .D(G_Pal_d));
  ROM #(.AddrBits(6), .Bits(8)) B_Pal (.A(VRAM_d[5:0]), .sel(1'b1), .D(B_Pal_d));
  VGA vga_1 (.R(R_Pal_d), .G(G_Pal_d), .B(B_Pal_d), .H(H), .V(V), .C(Pclk));

  // Other names for the same wires on the sheet: C = Clock

  // Notes on the sheet:
  //   Clock: pin W5, Hz: 50350000
  //   contents of R_Pal (hex, n*v repeats v):
  //   0,7e,c3,5*ff,a7,0,0,0,12,1d,a,29,83,ff,ff,d4,ab,74,42,5f,db,ff,ff
  //   ,bd,83,5f,a2,c2
  //   contents of G_Pal (hex, n*v repeats v):
  //   0,25,0,0,66,a3,ec,ff,f7,e4,b2,87,53,2b,62,ad,eb,f1,cc,8e,52,2f
  //   ,21,34,37,77,ac,9a,76,57,88,c3
  //   contents of B_Pal (hex, n*v repeats v):
  //   0,53,2e,4d,0,0,27,7d,35,36,51,51,59,53,be,ff,f5,e8,aa,6f,36,29
  //   ,36,7e,b8,a8,c5,df,9c,4f,79,c7
endmodule
