// Digital circuit VGA_top.dig as structural Verilog
module VGA_top (
  input  Clock
);

  wire d_ff_1_nq, H, Pclk, V, vga_sync_1_h_sync, vga_sync_1_v_sync;
  wire [5:0] vram_1_out_color;
  wire [7:0] B_Pal_d, G_Pal_d, R_Pal_d;
  wire [7:6] vram_1_out_color_2;
  wire [9:0] vga_sync_1_h_pixel, vga_sync_1_v_pixel;

  vga_sync vga_sync_1 (
    .en(1'b1), .H_neg(1'b1), .V_neg(1'b1), .Pclk(Pclk), .H_pixel(vga_sync_1_h_pixel),
    .V_pixel(vga_sync_1_v_pixel), .H_sync(vga_sync_1_h_sync), .V_sync(vga_sync_1_v_sync));
  D_FF d_ff_1 (.D(d_ff_1_nq), .C(Clock), .Q(Pclk), .nQ(d_ff_1_nq));
  Vram vram_1 (
    .X(vga_sync_1_h_pixel[8:0]), .Y(vga_sync_1_v_pixel[8:0]), .Clk(Pclk), .H_in(vga_sync_1_h_sync),
    .V_in(vga_sync_1_v_sync), .out_color({vram_1_out_color_2, vram_1_out_color}), .H_out(H), .V_out(V));
  ROM #(.AddrBits(6), .Bits(8)) R_Pal (.A(vram_1_out_color), .sel(1'b1), .D(R_Pal_d));
  ROM #(.AddrBits(6), .Bits(8)) G_Pal (.A(vram_1_out_color), .sel(1'b1), .D(G_Pal_d));
  ROM #(.AddrBits(6), .Bits(8)) B_Pal (.A(vram_1_out_color), .sel(1'b1), .D(B_Pal_d));
  VGA vga_1 (.R(R_Pal_d), .G(G_Pal_d), .B(B_Pal_d), .H(H), .V(V), .C(Pclk));

  // Other names for the same wires on the sheet: C = Clock

  // Notes on the sheet:
  //   Clock: pin W5, Hz: 18018000
  //   contents of R_Pal (hex, n*v repeats v):
  //   0,7e,c3,5*ff,a7,0,0,0,12,1d,a,29,83,ff,ff,d4,ab,74,42,5f,db,ff,ff
  //   ,bd,83,5f,a2,c2
  //   contents of G_Pal (hex, n*v repeats v):
  //   0,25,0,0,66,a3,ec,ff,f7,e4,b2,87,53,2b,62,ad,eb,f1,cc,8e,52,2f
  //   ,21,34,37,77,ac,9a,76,57,88,c3
  //   contents of B_Pal (hex, n*v repeats v):
  //   0,53,2e,4d,0,0,27,7d,35,36,51,51,59,53,be,ff,f5,e8,aa,6f,36,29
  //   ,36,7e,b8,a8,c5,df,9c,4f,79,c7
endmodule
