// Digital circuit Vram.dig as structural Verilog
module Vram (
  input  [8:0] X,
  input  [8:0] Y,
  input  Clk,
  input  H_in,
  input  V_in,
  output [7:0] out_color,
  output H_out,
  output V_out
);

  wire [7:0] VRAM_d;
  wire [17:0] add_1_s, mul_1_mul;

  Mul #(.Bits(9)) mul_1 (.a(9'h1e0), .b(Y), .mul(mul_1_mul));
  D_FF d_ff_1 (.D(H_in), .C(Clk), .Q(H_out));  // open: nQ
  D_FF d_ff_2 (.D(V_in), .C(Clk), .Q(V_out));  // open: nQ
  Add #(.Bits(18)) add_1 (.a({{9{1'b0}}, X}), .b(mul_1_mul), .c_i(1'b0), .s(add_1_s));  // open: c_o
  RAMDualPort #(.AddrBits(18), .isProgramMemory("true"), .Bits(8)) VRAM (
    .A(add_1_s), .Din({8{1'b0}}), .str(1'b0), .C(Clk), .ld(1'b1), .D(VRAM_d));
  D_FF #(.Bits(8)) d_ff_3 (.D(VRAM_d), .C(Clk), .Q(out_color));  // open: nQ

  // Other names for the same wires on the sheet: C = Clk

  // Notes on the sheet:
  //   Clk: Hz: 48
endmodule
