// Digital circuit equals.dig as structural Verilog
module equals (
  input  A,
  input  B,
  output Q
);

  Comparator #(.generic("this.Bits = args.bitWidth;")) eq (.a(A), .b(B), .eq(Q));  // open: gt, lt
endmodule

/* Code that sets the parameters or builds the circuit:
bitWidth := 8;
*/
