// Digital circuit vga_sync.dig as structural Verilog
module vga_sync (
  input  en,
  input  H_neg,
  input  V_neg,
  input  Pclk,
  output [9:0] H_pixel,
  output [9:0] V_pixel,
  output H_sync,
  output V_sync
);

  wire equals_1_q, equals_2_q, equals_3_q, equals_4_q, equals_5_q, equals_6_q, jk_ff_1_nq, jk_ff_2_nq;
  wire [9:0] sub_1_s, sub_2_s, sub_3_s, sub_4_s, sub_5_s, sub_6_s, sub_7_s, sub_8_s;

  Sub #(.Bits(10)) sub_1 (.a(10'h1e0), .b(10'h1), .c_i(1'b0), .s(sub_1_s));  // open: c_o
  Sub #(.Bits(10)) sub_2 (.a({10{1'b0}}), .b(10'h2), .c_i(1'b0), .s(sub_2_s));  // open: c_o
  Sub #(.Bits(10)) sub_3 (.a(sub_2_s), .b(10'h29), .c_i(1'b0), .s(sub_3_s));  // open: c_o
  Sub #(.Bits(10)) sub_4 (.a(sub_3_s), .b(10'h2), .c_i(1'b0), .s(sub_4_s));  // open: c_o
  Sub #(.Bits(10)) sub_5 (.a(10'h110), .b(10'h1), .c_i(1'b0), .s(sub_5_s));  // open: c_o
  Sub #(.Bits(10)) sub_6 (.a({10{1'b0}}), .b(10'h2), .c_i(1'b0), .s(sub_6_s));  // open: c_o
  Sub #(.Bits(10)) sub_7 (.a(sub_6_s), .b(10'ha), .c_i(1'b0), .s(sub_7_s));  // open: c_o
  Sub #(.Bits(10)) sub_8 (.a(sub_7_s), .b(10'h2), .c_i(1'b0), .s(sub_8_s));  // open: c_o
  equals #(.generic("bitWidth := 10;")) equals_1 (.A(H_pixel), .B(sub_1_s), .Q(equals_1_q));
  equals #(.generic("bitWidth := 10;")) equals_2 (.A(H_pixel), .B(sub_2_s), .Q(equals_2_q));
  equals #(.generic("bitWidth := 10;")) equals_3 (.A(H_pixel), .B(sub_3_s), .Q(equals_3_q));
  equals #(.generic("bitWidth := 10;")) equals_4 (.A(V_pixel), .B(sub_5_s), .Q(equals_4_q));
  equals #(.generic("bitWidth := 10;")) equals_5 (.A(V_pixel), .B(sub_6_s), .Q(equals_5_q));
  equals #(.generic("bitWidth := 10;")) equals_6 (.A(V_pixel), .B(sub_7_s), .Q(equals_6_q));
  JK_FF jk_ff_1 (.J(equals_3_q), .C(Pclk), .K(equals_2_q), .nQ(jk_ff_1_nq));  // open: Q
  JK_FF jk_ff_2 (.J(equals_6_q), .C(Pclk), .K(equals_5_q), .nQ(jk_ff_2_nq));  // open: Q
  CounterPreset #(.Bits(10)) counterpreset_1 (
    .en(en), .C(Pclk), .dir(1'b0), .in(sub_4_s), .ld(equals_1_q), .clr(1'b0), .out(H_pixel));  // open: ovf
  CounterPreset #(.Bits(10)) counterpreset_2 (
    .en(en), .C(equals_1_q), .dir(1'b0), .in(sub_8_s), .ld(equals_4_q), .clr(1'b0), .out(V_pixel));  // open: ovf
  xnor xnor_1 (H_sync, jk_ff_1_nq, H_neg);
  xnor xnor_2 (V_sync, jk_ff_2_nq, V_neg);

  // Notes on the sheet:
  //   en: default 1
  //   Pclk: Hz: 2800
endmodule
