// Digital circuit vga_timing.dig as structural Verilog
module vga_timing (
  input  Pclk,
  input  [8:0] res,
  input  [8:0] fp,
  input  [8:0] sync,
  input  [8:0] bp,
  input  neg,
  input  clock,
  input  en,
  output [8:0] V,
  output pulse,
  output next
);

  wire comparator_2_eq, comparator_3_eq, jk_ff_1_nq;
  wire [8:0] sub_1_s, sub_2_s, sub_3_s, sub_4_s;

  Sub #(.Bits(9)) sub_1 (.a(res), .b(9'h1), .c_i(1'b0), .s(sub_1_s));  // open: c_o
  Sub #(.Bits(9)) sub_2 (.a({9{1'b0}}), .b(bp), .c_i(1'b0), .s(sub_2_s));  // open: c_o
  Sub #(.Bits(9)) sub_3 (.a(sub_2_s), .b(sync), .c_i(1'b0), .s(sub_3_s));  // open: c_o
  Sub #(.Bits(9)) sub_4 (.a(sub_3_s), .b(fp), .c_i(1'b0), .s(sub_4_s));  // open: c_o
  Comparator #(.Signed("true"), .Bits(9)) comparator_1 (.a(V), .b(sub_1_s), .eq(next));  // open: gt, lt
  Comparator #(.Signed("true"), .Bits(9)) comparator_2 (.a(V), .b(sub_2_s), .eq(comparator_2_eq));  // open: gt, lt
  Comparator #(.Signed("true"), .Bits(9)) comparator_3 (.a(V), .b(sub_3_s), .eq(comparator_3_eq));  // open: gt, lt
  JK_FF jk_ff_1 (.J(comparator_3_eq), .C(Pclk), .K(comparator_2_eq), .nQ(jk_ff_1_nq));  // open: Q
  CounterPreset #(.Bits(9)) counterpreset_1 (
    .en(en), .C(Pclk), .dir(1'b0), .in(sub_4_s), .ld(next), .clr(1'b0), .out(V));  // open: ovf
  xnor xnor_1 (pulse, jk_ff_1_nq, neg);

  // Other names for the same wires on the sheet: Clk = clock

  // Notes on the sheet:
  //   res: default 26
  //   fp: default 8
  //   sync: default 12
  //   bp: default 8
  //   en: default 1
endmodule
